# Fritzing sketch sketch (saved by Fritzing 1.0.1rc)

parts:
  Mod1 = Raspberry Pi 4B
  J1 = Basic Servo
  J2 = Basic Servo
  Part1 = Adafruit PCA9685 PWM/Servo Breakout [part_number=815]
  VCC1 = 4 x AAA Battery Mount
  J3 = Generic female header - 1 pins [form="♀ (female)" package=THT]  # not connected

nets:
  5V: Mod1.5V, Part1.VCC
  N1: Mod1.GPIO2, Part1.SCL
  N2: Mod1.GPIO3, Part1.SDA
  GND: Mod1.GND, J1.gnd, J2.gnd, Part1.GND, VCC1.+
  VCC: J1.vcc, J2.vcc, Part1.5.0V
  N3: J1.pulse, Part1.PWM0
  N4: J2.pulse, Part1.PWM1
  N5: Part1.PWRIN, VCC1.-

notes:
  horizontal movement
  vertical movement
  Motor power
  RPi for servo and camera control scripts
  servo driver PCA9685
  USB Camera

custom parts:
  Adafruit PCA9685 PWM/Servo Breakout: Using only two pins, control 16 free-running PWM outputs! I2C-controlled PWM driver with a built in clock. Unlike the TLC5940 family, you do not need to continuously send it signal tying up your microcontroller, its completely free running! 5V compliant, which means you can control it from a 3.3V microcontroller and still safely drive up to 6V outputs (this is good for when you want to control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
  Generic female header - 1 pins: Generic female header
